# Fritzing sketch circuit (saved by Fritzing 0.9.3b)
circuit board: 10cm x 7cm
breadboards: 1

parts:
  P1 = Arduino Nano (Rev3.0)
  VCC = Battery block 9V
  P2 = Bluetooth HC-05 Macho
  P3 = Parallax 2-Axis Joystick
  R1 = Resistor [tolerance=±5% resistance=2.2k package=THT]
  R2 = Resistor [tolerance=±5% resistance=1k package=THT]

nets:
  GND: P1.GND, VCC.-, P2.GND, P3.GND, R1.Pin_0
  N1: P1.D2, P2.TXD
  N2: P1.D3, R1.Pin_1, R2.Pin_0
  N3: P1.VIN, VCC.+
  5V: P1.5V, P2.VCC, P3.L/R_Vcc, P3.U/D_Vcc
  N4: P1.A4, P3.L/R_Out
  N5: P1.A3, P3.U/D_Out
  N6: P2.RXD, R2.Pin_1

custom parts:
  Parallax 2-Axis Joystick: Description: This is the Parallax 2-Axis Joystick. It contains a spring return thumb joystick mounted to a breakout board. The breakout board breaks out the joysticks connections to .1" pin headers. The joystick's connections are duplicated on both sides of the board for easy use. This part can easily be used on a breadboard due to the .1" pin headers, but can also be soldered into any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
