# Fritzing sketch circuit (saved by Fritzing 0.9.3b)
circuit board: 10cm x 7cm
breadboards: 1

parts:
  VCC = Battery block 9V
  P2 = Bluetooth HC-05 Macho
  R1 = Resistor [tolerance=±5% resistance=2.2k package=THT]
  R2 = Resistor [tolerance=±5% resistance=1k package=THT]
  M1 = DC Motor
  M2 = DC Motor
  P1 = Arduino Nano (Rev3.0)
  L9110H_-_2 = L9110H [package="DIP (Dual Inline) [THT]"]
  L9110H_-_1 = L9110H [package="DIP (Dual Inline) [THT]"]

nets:
  GND: VCC.-, P2.GND, R1.Pin_0, P1.GND, L9110H_-_2.GND, L9110H_-_1.GND
  9V: VCC.+, P1.VIN, L9110H_-_2.VCC, L9110H_-_1.VCC
  N1: P2.TXD, P1.D2
  N2: P2.RXD, R2.Pin_1
  5V: P2.VCC, P1.5V
  N3: R1.Pin_1, R2.Pin_0, P1.D3
  N4: M1.pin_1, L9110H_-_1.OB
  N5: M1.pin_2, L9110H_-_1.OA
  N6: M2.pin_1, L9110H_-_2.OB
  N7: M2.pin_2, L9110H_-_2.OA
  D4: P1.D4, L9110H_-_1.IB
  D5: P1.D5, L9110H_-_1.IA
  D6: P1.D6, L9110H_-_2.IB
  D7: P1.D7, L9110H_-_2.IA

custom parts:
  L9110H: The ASIC device control and drive motor design two-channel push-pull power amplifier discrete circuits integrated into a monolithic IC, peripheral devices and reduce the cost, improve the reliability of the whole. This chip has two TTL / CMOS compatible with the level of the input, with good resistance; two output terminals can directly forward and reverse movement of the drive motor, it has a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
