# Fritzing sketch circuit (saved by Fritzing 0.9.3b)
circuit board: 10cm x 7cm
breadboards: 1

parts:
  P1 = Arduino Nano (Rev3.0)
  VCC = Battery block 9V
  P2 = NRF24L01+ Breakout Board

nets:
  GND: P1.GND, VCC.-, P2.GND
  D9: P1.D9, P2.CE
  D10: P1.D10, P2.CS
  D11: P1.D11/MOSI, P2.MOSI
  D12: P1.D12/MISO, P2.MISO
  VIN: P1.VIN, VCC.+
  3.3V: P1.3V3, P2.VCC
  D13: P1.D13/SCK, P2.SCK
